// Logisim project imm-gen.circ as structural Verilog: 1 circuit, main circuit imm_gen
module imm_gen (
  input  [31:0] Instruction,
  input  [2:0] ImmSel,
  output [31:0] Immediate
);

  assign Immediate[31:11] = {{20{Instruction[31]}}, Instruction[31]};  // Bit_Extender bit_extender_1

  assign Immediate[10:0] = Instruction[30:20];

  // Other names for the same wires on the sheet: I_type0[31:0] = {Immediate[31:11], Instruction[30:20]}

  // Notes on the sheet:
  //   INPUTS to your circuit
  //   DON'T CHANGE THE LOCATIONS OF THE INPUTS AND OUTPUTS!
  //   OUTPUT from your circuit
endmodule
